// Logisim project ALU.circ as structural Verilog: 2 circuits, main circuit ALU
module ALU (
  input  [31:0] A,
  input  [31:0] B,
  input  [4:0] Shift,
  input  [3:0] Codop,
  input  CarryIn,
  output [31:0] S,
  output [3:0] Flags
);

  wire bitselector_1_out, bitselector_2_out, CADC, CASR, CCMN, CCMP, CLSL, CSBC, DernierBitSort, not_1_out,
       not_3_out, ShiftNul, VADC, VCMP, VRSB, xnor_1_out, xor_2_out, xor_3_out, xor_4_out;
  wire [4:0] subtractor_3_out, subtractor_4_out;
  wire [30:0] sortieF;
  wire [31:0] ADC, adder_3_out, ANDD, ASR, BIC, bit_extender_1_out, CMN, CMP, EOR, LSL, LSR, MUL, MVN, ORR,
       RORR, RSB, SBC;

  not not_1 (not_1_out, CarryIn);
  assign ANDD = A & B;  // AND_Gate and_1, 32 bits wide
  assign EOR = A ^ B;  // XOR_Gate xor_1, 32 bits wide
  Shifter #(.width(32)) shifter_1 (.in(B), .\dist (Shift), .out(LSL));
  Shifter #(.shift("lr"), .width(32)) shifter_2 (.in(B), .\dist (Shift), .out(LSR));
  Shifter #(.shift("ar"), .width(32)) shifter_3 (.in(B), .\dist (Shift), .out(ASR));
  Adder #(.width(32)) adder_1 (.a(A), .b(B), .out(ADC), .cin(CarryIn), .cout(CADC));
  Subtractor #(.width(32)) subtractor_1 (.a(B), .b(A), .out(SBC), .bin(not_1_out));  // open: bout
  Shifter #(.shift("rr"), .width(32)) shifter_4 (.in(B), .\dist (Shift), .out(RORR));
  Negator #(.width(32)) negator_1 (.in(A), .out(RSB));
  Subtractor #(.width(32)) subtractor_2 (.a(B), .b(A), .out(CMP), .bout(CCMP));  // open: bin
  Adder #(.width(32)) adder_2 (.a(A), .b(B), .out(CMN), .cout(CCMN));  // open: cin
  assign ORR = A | B;  // OR_Gate or_1, 32 bits wide
  Multiplier #(.width(32)) multiplier_1 (.a(A), .b(B), .out(MUL));  // open: cin, cout
  assign BIC = ~A & B;  // AND_Gate and_2, 32 bits wide
  assign MVN = ~A;  // NOT_Gate not_2, 32 bits wide
  not not_3 (not_3_out, CarryIn);
  assign bit_extender_1_out = {{31{1'b0}}, not_3_out};  // Bit_Extender bit_extender_1
  Multiplexer #(.enable("true"), .select(4), .width(32)) multiplexer_1 (
    .in0(ANDD), .in1(EOR), .in2(LSL), .in3(LSR), .in4(ASR), .in5(ADC), .in6(SBC), .in7(RORR), .in8(B),
    .in9(RSB), .in10(B), .in11(B), .in12(ORR), .in13(MUL), .in14(BIC), .in15(MVN), .out(S), .sel(Codop),
    .en(1'b1));
  Multiplexer #(.enable("true"), .select(4), .width(32)) multiplexer_2 (
    .in0(ANDD), .in1(EOR), .in2(LSL), .in3(LSR), .in4(ASR), .in5(ADC), .in6(SBC), .in7(RORR), .in8(ANDD),
    .in9(RSB), .in10(CMP), .in11(CMN), .in12(ORR), .in13(MUL), .in14(BIC), .in15(MVN),
    .out({DernierBitSort, sortieF}), .sel(Codop), .en(1'b1));
  Multiplexer #(.enable("true"), .select(4)) multiplexer_3 (
    .in0(1'b0), .in1(1'b0), .in2(CLSL), .in3(CASR), .in4(CASR), .in5(CADC), .in6(CSBC), .in7(DernierBitSort),
    .in8(1'b0), .in9(1'b0), .in10(CCMP), .in11(CCMN), .in12(1'b0), .in13(1'b0), .in14(1'b0), .in15(1'b0),
    .out(Flags[1]), .sel(Codop), .en(1'b1));
  Multiplexer #(.enable("true"), .select(4)) multiplexer_4 (
    .in0(1'b0), .in1(1'b0), .in2(1'b0), .in3(1'b0), .in4(1'b0), .in5(VADC), .in6(VCMP), .in7(1'b0),
    .in8(1'b0), .in9(VRSB), .in10(VCMP), .in11(VADC), .in12(1'b0), .in13(1'b0), .in14(1'b0), .in15(1'b0),
    .out(Flags[0]), .sel(Codop), .en(1'b1));
  Adder #(.width(32)) adder_3 (.a(bit_extender_1_out), .b(A), .out(adder_3_out));  // open: cin, cout
  Comparator #(.mode("unsigned"), .width(32)) comparator_1 (.a(adder_3_out), .b(B), .gt(CSBC));  // open: eq, lt
  Comparator #(.width(32)) comparator_2 (
    .a({32{1'b0}}), .b({DernierBitSort, sortieF}), .gt(Flags[3]), .eq(Flags[2]));  // open: lt
  Comparator #(.mode("unsigned"), .width(5)) comparator_3 (.a({5{1'b0}}), .b(Shift), .eq(ShiftNul));  // open: gt, lt
  Subtractor #(.width(5)) subtractor_3 (.a({5{1'b0}}), .b(Shift), .out(subtractor_3_out));  // open: bin, bout
  Subtractor #(.width(5)) subtractor_4 (.a(Shift), .b(5'b00001), .out(subtractor_4_out));  // open: bin, bout
  xor xor_2 (xor_2_out, A[31], DernierBitSort);
  BitSelector #(.width(32)) bitselector_1 (.in(B), .out(bitselector_1_out), .sel(subtractor_3_out));
  Multiplexer multiplexer_5 (.in0(bitselector_1_out), .in1(1'b0), .out(CLSL), .sel(ShiftNul));
  BitSelector #(.width(32)) bitselector_2 (.in(B), .out(bitselector_2_out), .sel(subtractor_4_out));
  Multiplexer multiplexer_6 (.in0(bitselector_2_out), .in1(1'b0), .out(CASR), .sel(ShiftNul));
  xor xor_3 (xor_3_out, A[31], B[31]);
  and and_3 (VCMP, xor_3_out, xor_4_out);
  xor xor_4 (xor_4_out, B[31], DernierBitSort);
  xnor xnor_1 (xnor_1_out, B[31], A[31]);
  and and_4 (VADC, xnor_1_out, xor_2_out);
  xnor xnor_2 (VRSB, A[31], DernierBitSort);

  // Other names for the same wires on the sheet: DBSA = A[31]; DBSB = B[31]; CLSR = CASR; V = Flags[0]; C = Flags[1];
  //   Z = Flags[2]; N = Flags[3]; KARIN = CarryIn; sortieF[31] = DernierBitSort; sortieM[31:0] = S; VCMN = VADC;
  //   VSBC = VCMP
endmodule

module OP (
  input  [3:0] codop,
  input  AxorB,
  input  BLshift,
  input  BRshift,
  input  BRshiftA,
  input  AplusBplusCin,
  input  BminusAplusCinMinusONE,
  input  BRshiftR,
  input  AanddB,
  input  ZEROminusA,
  input  BminusA,
  input  AplusB,
  input  AorB,
  input  AfoisB,
  input  BandnotA,
  input  notA,
  output AandB
);

  wire not_1_out, not_2_out, not_3_out, not_4_out;

  not not_1 (not_1_out, codop[3]);
  not not_2 (not_2_out, codop[2]);
  not not_3 (not_3_out, codop[1]);
  not not_4 (not_4_out, codop[0]);
  and and_1 (AandB, not_1_out, not_2_out, not_3_out, not_4_out);
  and and_2 (AxorB, not_1_out, not_2_out, not_3_out, codop[0]);
  and and_3 (BLshift, not_1_out, not_2_out, codop[1], not_4_out);
  and and_4 (BRshift, not_1_out, not_2_out, codop[1], codop[0]);
  and and_5 (BRshiftA, not_1_out, codop[2], not_3_out, not_4_out);
  and and_6 (AplusBplusCin, not_1_out, codop[2], not_3_out, codop[0]);
  and and_7 (BminusAplusCinMinusONE, not_1_out, codop[2], codop[1], not_4_out);
  and and_8 (BRshiftR, not_1_out, codop[2], codop[1], codop[0]);
  and and_9 (AanddB, codop[3], not_2_out, not_3_out, not_4_out);
  and and_10 (ZEROminusA, codop[3], not_2_out, not_3_out, codop[0]);
  and and_11 (BminusA, codop[3], not_2_out, codop[1], not_4_out);
  and and_12 (AplusB, codop[3], not_2_out, codop[1], codop[0]);
  and and_13 (AorB, codop[3], codop[2], not_3_out, not_4_out);
  and and_14 (AfoisB, codop[3], codop[2], not_3_out, codop[0]);
  and and_15 (BandnotA, codop[3], codop[2], codop[1], not_4_out);
  and and_16 (notA, codop[3], codop[2], codop[1], codop[0]);
endmodule
