// Logisim project ALUHabib.circ as structural Verilog: 3 circuits, main circuit ALU
module ALU (
  input  [31:0] A,
  input  [31:0] B,
  input  [4:0] Shift,
  input  [3:0] Codop,
  input  CarryIn,
  output [31:0] S,
  output [3:0] Flags
);

  wire and_4_out, DernierBitSort, KAROUTMOINS, KAROUTMOINSnul, KAROUTPLUS, KAROUTPLUSnul, not_3_out,
       OverflowM, OverflowMC, OverflowP, OverflowPC, OverflowZMA, subtractor_2_bout, xnor_1_out, xnor_2_out,
       xor_4_out, xor_5_out;
  wire [30:0] sortieF;
  wire [31:0] AandB, AfoisB, AminusBplusCinminusONE, AORB, AplusB, AplusBplusCin, AxorB, BandnotA, BLshift,
       BminusA, BRshift, BRshiftA, BRshiftR, not_1_out, notA, ZEROminusA;

  Negator #(.width(32)) negator_1 (.in(A), .out(ZEROminusA));
  assign not_1_out = ~A;  // NOT_Gate not_1, 32 bits wide
  assign notA = ~A;  // NOT_Gate not_2, 32 bits wide
  assign AxorB = A ^ B;  // XOR_Gate xor_1, 32 bits wide
  Shifter #(.width(32)) shifter_1 (.in(B), .\dist (Shift), .out(BRshift));
  Shifter #(.shift("lr"), .width(32)) shifter_2 (.in(B), .\dist (Shift), .out(BLshift));
  Shifter #(.shift("ar"), .width(32)) shifter_3 (.in(B), .\dist (Shift), .out(BRshiftA));
  Shifter #(.shift("rr"), .width(32)) shifter_4 (.in(B), .\dist (Shift), .out(BRshiftR));
  Subtractor #(.width(32)) subtractor_1 (.a(B), .b(A), .out(BminusA), .bout(KAROUTMOINSnul));  // open: bin
  Adder #(.width(32)) adder_1 (.a(A), .b(B), .out(AplusB), .cout(KAROUTPLUSnul));  // open: cin
  Multiplier #(.width(32)) multiplier_1 (.a(A), .b(B), .out(AfoisB));  // open: cin, cout
  assign AORB = A | B;  // OR_Gate or_1, 32 bits wide
  assign BandnotA = not_1_out & B;  // AND_Gate and_1, 32 bits wide
  Adder #(.width(32)) adder_2 (.a(A), .b(B), .out(AplusBplusCin), .cin(CarryIn), .cout(KAROUTPLUS));
  assign AandB = A & B;  // AND_Gate and_2, 32 bits wide
  not not_3 (not_3_out, CarryIn);
  Subtractor #(.width(32)) subtractor_2 (
    .a(B), .b(A), .out(AminusBplusCinminusONE), .bin(not_3_out), .bout(subtractor_2_bout));
  not not_4 (KAROUTMOINS, subtractor_2_bout);
  Multiplexer #(.enable("true"), .select(4), .width(32)) multiplexer_1 (
    .in0(AandB), .in1(AxorB), .in2(BRshift), .in3(BLshift), .in4(BRshiftA), .in5(AplusBplusCin),
    .in6(AminusBplusCinminusONE), .in7(BRshiftR), .in8(B), .in9(ZEROminusA), .in10(B), .in11(B), .in12(AORB),
    .in13(AfoisB), .in14(BandnotA), .in15(notA), .out(S), .sel(Codop), .en(1'b1));
  Multiplexer #(.enable("true"), .select(4), .width(32)) multiplexer_2 (
    .in0(AandB), .in1(AxorB), .in2(BRshift), .in3(BLshift), .in4(BRshiftA), .in5(AplusBplusCin),
    .in6(AminusBplusCinminusONE), .in7(BRshiftR), .in8(AandB), .in9(ZEROminusA), .in10(BminusA),
    .in11(AplusB), .in12(AORB), .in13(AfoisB), .in14(BandnotA), .in15(notA), .out({DernierBitSort, sortieF}),
    .sel(Codop), .en(1'b1));
  Multiplexer #(.enable("true"), .select(4)) multiplexer_3 (
    .in0(1'b0), .in1(1'b0), .in2(DernierBitSort), .in3(DernierBitSort), .in4(DernierBitSort),
    .in5(KAROUTPLUS), .in6(KAROUTMOINS), .in7(DernierBitSort), .in8(1'b0), .in9(1'b0), .in10(KAROUTMOINSnul),
    .in11(KAROUTPLUSnul), .in12(1'b0), .in13(1'b0), .in14(1'b0), .in15(1'b0), .out(Flags[1]), .sel(Codop),
    .en(1'b1));
  xnor xnor_1 (xnor_1_out, A[31], DernierBitSort);
  Multiplexer #(.enable("true"), .select(4)) multiplexer_4 (
    .in0(1'b0), .in1(1'b0), .in2(1'b0), .in3(1'b0), .in4(1'b0), .in5(OverflowPC), .in6(OverflowMC),
    .in7(1'b0), .in8(1'b0), .in9(OverflowZMA), .in10(OverflowM), .in11(OverflowP), .in12(1'b0), .in13(1'b0),
    .in14(1'b0), .in15(1'b0), .out(Flags[0]), .sel(Codop), .en(1'b1));
  xor xor_2 (OverflowMC, CarryIn, KAROUTMOINS);
  and and_3 (OverflowZMA, A[31], xnor_1_out);
  xor xor_3 (OverflowPC, CarryIn, KAROUTPLUS);
  xnor xnor_2 (xnor_2_out, A[31], B[31]);
  and and_4 (and_4_out, Flags[3], A[31]);
  xor xor_4 (xor_4_out, A[31], B[31]);
  xor xor_5 (xor_5_out, Flags[3], A[31]);
  Comparator #(.width(32)) comparator_1 (
    .a({32{1'b0}}), .b({DernierBitSort, sortieF}), .gt(Flags[3]), .eq(Flags[2]));  // open: lt
  and and_5 (OverflowM, and_4_out, xor_4_out);
  and and_6 (OverflowP, xor_5_out, xnor_2_out);

  // Other names for the same wires on the sheet: DBSA = A[31]; DBSB = B[31]; V = Flags[0]; C = Flags[1]; Z = Flags[2];
  //   N = Flags[3]; KARIN = CarryIn; sortieF[31] = DernierBitSort; sortieM[31:0] = S
endmodule

module BancRegistre (
  input  [31:0] DataIn,
  input  [2:0] RegDest,
  input  Clk,
  input  Reset,
  input  [2:0] RegA,
  input  [2:0] RegB,
  output [31:0] BOut,
  output [31:0] AOut,
  output [31:0] R0,
  output [31:0] R1,
  output [31:0] R2,
  output [31:0] R3,
  output [31:0] R4,
  output [31:0] R5,
  output [31:0] R6,
  output [31:0] R7
);

  wire [31:0] AOUT_t, BOUT_t;

  Register #(.width(32)) register_1 (.D(DataIn), .en(1'b1), .clk(Clk), .Q(R0), .clr(Reset));
  Register #(.width(32)) register_2 (.D(DataIn), .en(1'b1), .clk(Clk), .Q(R1), .clr(Reset));
  Register #(.width(32)) register_3 (.D(DataIn), .en(1'b1), .clk(Clk), .Q(R2), .clr(Reset));
  Register #(.width(32)) register_4 (.D(DataIn), .en(1'b1), .clk(Clk), .Q(R3), .clr(Reset));
  Register #(.width(32)) register_5 (.D(DataIn), .en(1'b1), .clk(Clk), .Q(R4), .clr(Reset));
  Register #(.width(32)) register_6 (.D(DataIn), .en(1'b1), .clk(Clk), .Q(R5), .clr(Reset));
  Register #(.width(32)) register_7 (.D(DataIn), .en(1'b1), .clk(Clk), .Q(R6), .clr(Reset));
  Register #(.width(32)) register_8 (.D(DataIn), .en(1'b1), .clk(Clk), .Q(R7), .clr(Reset));
  Demultiplexer #(.enable("true"), .select(3), .width(32)) demultiplexer_1 (
    .out0(R0), .out1(R1), .out2(R2), .out3(R3), .out4(R4), .out5(R5), .out6(R6), .out7(R7), .in(DataIn),
    .sel(RegDest), .en(1'b1));
  Register #(.width(32)) register_9 (.D(AOUT_t), .en(1'b1), .clk(Clk), .Q(AOut), .clr(Reset));
  Multiplexer #(.enable("true"), .select(3), .width(32)) multiplexer_1 (
    .in0(R0), .in1(R1), .in2(R2), .in3(R3), .in4(R4), .in5(R5), .in6(R6), .in7(R7), .out(AOUT_t), .sel(RegA),
    .en(1'b1));
  Multiplexer #(.enable("true"), .select(3), .width(32)) multiplexer_2 (
    .in0(R0), .in1(R1), .in2(R2), .in3(R3), .in4(R4), .in5(R5), .in6(R6), .in7(R7), .out(BOUT_t), .sel(RegB),
    .en(1'b1));
  Register #(.width(32)) register_10 (.D(BOUT_t), .en(1'b1), .clk(Clk), .Q(BOut), .clr(Reset));

  // Other names for the same wires on the sheet: REGD[2:0] = RegDest; RST = Reset
endmodule

module OP (
  input  [3:0] codop,
  input  AandB,
  input  AxorB,
  input  BLshift,
  input  BRshift,
  input  BRshiftA,
  input  AplusBplusCin,
  input  BminusAplusCinMinusONE,
  input  BRshiftR,
  input  AanddB,
  input  ZEROminusA,
  input  BminusA,
  input  AplusB,
  input  AorB,
  input  AfoisB,
  input  BandnotA,
  input  notA
);

  wire not_1_out, not_2_out, not_3_out, not_4_out;

  not not_1 (not_1_out, codop[3]);
  not not_2 (not_2_out, codop[2]);
  not not_3 (not_3_out, codop[1]);
  not not_4 (not_4_out, codop[0]);
  and and_1 (AandB, not_1_out, not_2_out, not_3_out, not_4_out);
  and and_2 (AxorB, not_1_out, not_2_out, not_3_out, codop[0]);
  and and_3 (BLshift, not_1_out, not_2_out, codop[1], not_4_out);
  and and_4 (BRshift, not_1_out, not_2_out, codop[1], codop[0]);
  and and_5 (BRshiftA, not_1_out, codop[2], not_3_out, not_4_out);
  and and_6 (AplusBplusCin, not_1_out, codop[2], not_3_out, codop[0]);
  and and_7 (BminusAplusCinMinusONE, not_1_out, codop[2], codop[1], not_4_out);
  and and_8 (BRshiftR, not_1_out, codop[2], codop[1], codop[0]);
  and and_9 (AanddB, codop[3], not_2_out, not_3_out, not_4_out);
  and and_10 (ZEROminusA, codop[3], not_2_out, not_3_out, codop[0]);
  and and_11 (BminusA, codop[3], not_2_out, codop[1], not_4_out);
  and and_12 (AplusB, codop[3], not_2_out, codop[1], codop[0]);
  and and_13 (AorB, codop[3], codop[2], not_3_out, not_4_out);
  and and_14 (AfoisB, codop[3], codop[2], not_3_out, codop[0]);
  and and_15 (BandnotA, codop[3], codop[2], codop[1], not_4_out);
  and and_16 (notA, codop[3], codop[2], codop[1], codop[0]);
endmodule
