// Logisim project ALUHannah.circ as structural Verilog
module ALU (
  input  [31:0] A,
  input  [31:0] B,
  input  [4:0] Shift,
  input  [3:0] Codop,
  input  CarryIn,
  output [31:0] S,
  output [3:0] Flags
);

  wire adder_3_cout, not_3_out, not_4_out, subtractor_2_bout;
  wire [3:0] adder_1_out;
  wire [31:0] adder_2_out, and_2_out, and_3_out, and_4_out, negator_2_out, not_1_out, not_2_out, or_1_out,
       shifter_2_out, shifter_3_out, shifter_5_out, shifter_6_out, undriven, xor_1_out;

  Adder #(.width(4)) adder_1 (.out(adder_1_out));  // open: a, b, cin, cout
  Subtractor #(.width(4)) subtractor_1 (.out(adder_1_out));  // open: a, b, bin, bout
  Multiplier #(.width(4)) multiplier_1 (.out(adder_1_out));  // open: a, b, cin, cout
  Divider divider_1 ();  // open: a, b, out, upper, rem
  Negator negator_1 ();  // open: in, out
  Comparator #(.width(32)) comparator_1 ();  // open: a, b, gt, eq, lt
  Shifter shifter_1 ();  // open: in, dist, out
  BitAdder bitadder_1 ();  // open: in0, out
  BitFinder bitfinder_1 ();  // open: in, index, found
  FPAdder fpadder_1 ();  // open: a, b, out
  FPSubtractor fpsubtractor_1 ();  // open: a, b, out
  FPMultiplier fpmultiplier_1 ();  // open: a, b, out
  FPDivider fpdivider_1 ();  // open: a, b, out
  // FPNegator fpnegator_1: pin names not known
  // FPComparator fpcomparator_1: pin names not known
  // FPToInt fptoint_1: pin names not known
  // IntToFP inttofp_1: pin names not known
  // AND_Gate and_1 is placed but not wired
  assign not_1_out = ~A;  // NOT_Gate not_1, 32 bits wide
  assign and_2_out = A & B;  // AND_Gate and_2, 32 bits wide
  assign xor_1_out = A ^ B;  // XOR_Gate xor_1, 32 bits wide
  Shifter #(.width(32)) shifter_2 (.in(B), .\dist (Shift), .out(shifter_2_out));
  Shifter #(.shift("lr"), .width(32)) shifter_3 (.in(B), .\dist (Shift), .out(shifter_3_out));
  Shifter #(.shift("lr"), .width(32)) shifter_4 (.in(B), .\dist (Shift), .out(shifter_3_out));
  Shifter #(.shift("ar"), .width(32)) shifter_5 (.in(B), .\dist (Shift), .out(shifter_5_out));
  Shifter #(.shift("rr"), .width(32)) shifter_6 (.in(B), .\dist (Shift), .out(shifter_6_out));
  Shifter #(.shift("rr"), .width(32)) shifter_7 (.in(B), .\dist (Shift), .out(shifter_6_out));
  assign and_3_out = A & B;  // AND_Gate and_3, 32 bits wide
  Negator #(.width(32)) negator_2 (.in(A), .out(negator_2_out));
  assign or_1_out = A | B;  // OR_Gate or_1, 32 bits wide
  assign and_4_out = not_1_out & B;  // AND_Gate and_4, 32 bits wide
  assign not_2_out = ~A;  // NOT_Gate not_2, 32 bits wide
  Adder #(.width(32)) adder_2 (.a(A), .b(A), .out(adder_2_out));  // open: cin, cout
  Adder #(.width(32)) adder_3 (.a(undriven), .b(undriven), .cout(adder_3_cout));  // open: out, cin
  Multiplexer #(.select(4), .width(32)) multiplexer_1 (
    .in0(and_2_out), .in1(xor_1_out), .in2(shifter_2_out), .in3(shifter_3_out), .in4(shifter_5_out),
    .in5(shifter_6_out), .in6(and_3_out), .in7(negator_2_out), .in8(or_1_out), .in9(and_4_out),
    .in10(not_2_out), .in11(adder_2_out));  // open: in12, in13, in14, in15, out, sel
  not not_3 (not_3_out, CarryIn);
  Subtractor subtractor_2 (.bin(not_3_out), .bout(subtractor_2_bout));  // open: a, b, out
  not not_4 (not_4_out, subtractor_2_bout);

  // Notes on the sheet:
  //   Note: for ROR, C = N
  //   Note 2: assume that shift > 0 for LSL and LSR
  //   0-A
endmodule
