// Logisim project ALUKevin.circ as structural Verilog: 3 circuits, main circuit ALU
module ALU (
  input  [31:0] A,
  input  [31:0] B,
  input  [4:0] Shift,
  input  [3:0] in_4,
  input  CarryIn,
  output [31:0] S,
  output [3:0] Flags
);

  wire not_1_out, not_2_out, subtractor_1_bout, undriven;
  wire [3:0] CODOP;
  wire [31:0] adder_1_out, adder_2_out, and_1_out, controlled_inverter_1_out, controlled_inverter_2_out,
       EOR_out, multiplier_1_out, negator_1_out, ORR_out, shifter_1_out, shifter_2_out, shifter_3_out,
       shifter_4_out, subtractor_1_out, subtractor_2_out, TST;

  CODOP codop_1 (.a(in_4));  // open: AN, EOR, LSL, LSR, ASR, ADC, SBC, RORr, TST, RSB, CMP, CMN, ORR, MUL, BIC, MVN
  not not_1 (not_1_out, undriven);
  not not_2 (not_2_out, subtractor_1_bout);
  assign TST = A & B;  // AND_Gate AN, 32 bits wide
  assign EOR_out = A ^ B;  // XOR_Gate EOR, 32 bits wide
  Shifter #(.width(32)) shifter_1 (.in(B), .\dist (Shift), .out(shifter_1_out));
  Shifter #(.shift("lr"), .width(32)) shifter_2 (.in(B), .\dist (Shift), .out(shifter_2_out));
  Shifter #(.shift("ar"), .width(32)) shifter_3 (.in(B), .\dist (Shift), .out(shifter_3_out));
  Adder #(.width(32)) adder_1 (.a(A), .b(B), .out(adder_1_out));  // open: cin, cout
  Subtractor #(.width(32)) subtractor_1 (
    .a(A), .b(B), .out(subtractor_1_out), .bin(not_1_out), .bout(subtractor_1_bout));
  Shifter #(.shift("rr"), .width(32)) shifter_4 (.in(B), .\dist (Shift), .out(shifter_4_out));
  Negator #(.width(32)) negator_1 (.in(A), .out(negator_1_out));
  Subtractor #(.width(32)) subtractor_2 (.a(B), .b(A), .out(subtractor_2_out));  // open: bin, bout
  Adder #(.width(32)) adder_2 (.a(A), .b(B), .out(adder_2_out));  // open: cin, cout
  assign ORR_out = A | B;  // OR_Gate ORR, 32 bits wide
  Multiplier #(.width(32)) multiplier_1 (.a(A), .b(B), .out(multiplier_1_out));  // open: cin, cout
  Controlled_Inverter #(.width(32)) controlled_inverter_1 (.in(A), .out(controlled_inverter_1_out));  // open: en
  Controlled_Inverter #(.width(32)) controlled_inverter_2 (.in(A), .out(controlled_inverter_2_out));  // open: en
  assign and_1_out = controlled_inverter_1_out & B;  // AND_Gate and_1, 32 bits wide
  Multiplexer #(.select(4), .width(32)) multiplexer_1 (
    .in0(TST), .in1(EOR_out), .in2(shifter_1_out), .in3(shifter_2_out), .in4(shifter_3_out),
    .in5(adder_1_out), .in6(subtractor_1_out), .in7(shifter_4_out), .in8(TST), .in9(negator_1_out),
    .in10(subtractor_2_out), .in11(adder_2_out), .in12(ORR_out), .in13(multiplier_1_out), .in14(and_1_out),
    .in15(controlled_inverter_2_out), .sel(CODOP));  // open: out

  // Notes on the sheet:
  //   Note: for ROR, C = N
  //   Note 2: assume that shift > 0 for LSL and LSR
endmodule

module BancRegistre (
  input  [31:0] DataIn,
  input  [2:0] RegA,
  input  [2:0] RegB,
  input  [2:0] RegDest,
  input  Clk,
  input  Reset,
  output [31:0] AOut,
  output [31:0] BOut,
  output [31:0] R0,
  output [31:0] R1,
  output [31:0] R2,
  output [31:0] R3,
  output [31:0] R4,
  output [31:0] R5,
  output [31:0] R6,
  output [31:0] R7
);

  ALU alu_1 ();  // open: A, B, Shift, in_4, CarryIn, S, Flags
endmodule

module CODOP (
  input  [3:0] a,
  output AN,
  output EOR,
  output LSL,
  output LSR,
  output ASR,
  output ADC,
  output SBC,
  output RORr,
  output TST,
  output RSB,
  output CMP,
  output CMN,
  output ORR,
  output MUL,
  output BIC,
  output MVN
);

  wire not_1_out, not_2_out, not_3_out, not_4_out;

  not not_1 (not_1_out, a[3]);
  not not_2 (not_2_out, a[2]);
  not not_3 (not_3_out, a[1]);
  not not_4 (not_4_out, a[0]);
  and and_1 (AN, not_1_out, not_2_out, not_3_out, not_4_out);
  and and_2 (EOR, not_1_out, not_2_out, not_3_out, a[0]);
  and and_3 (LSL, not_1_out, not_2_out, a[1], not_4_out);
  and and_4 (LSR, not_1_out, not_2_out, a[1], a[0]);
  and and_5 (ASR, not_1_out, a[2], not_3_out, not_4_out);
  and and_6 (ADC, not_1_out, a[2], not_3_out, a[0]);
  and and_7 (SBC, not_1_out, a[2], a[1], not_4_out);
  and and_8 (RORr, not_1_out, a[2], a[1], a[0]);
  and and_9 (TST, a[3], not_2_out, not_3_out, not_4_out);
  and and_10 (RSB, a[3], not_2_out, not_3_out, a[0]);
  and and_11 (CMP, a[3], not_2_out, a[1], not_4_out);
  and and_12 (CMN, a[3], not_2_out, a[1], a[0]);
  and and_13 (ORR, a[3], a[2], not_3_out, not_4_out);
  and and_14 (MUL, a[3], a[2], not_3_out, a[0]);
  and and_15 (BIC, a[3], a[2], a[1], not_4_out);
  and and_16 (MVN, a[3], a[2], a[1], a[0]);
endmodule
