// Logisim project BancDeRegistres.circ as structural Verilog: 1 circuit, main circuit BancRegistre
module BancRegistre (
  input  [31:0] DataIn,
  input  [2:0] RegDest,
  input  Clk,
  input  Reset,
  input  [2:0] RegA,
  input  [2:0] RegB,
  output [31:0] BOut,
  output [31:0] AOut,
  output [31:0] R0,
  output [31:0] R1,
  output [31:0] R2,
  output [31:0] R3,
  output [31:0] R4,
  output [31:0] R5,
  output [31:0] R6,
  output [31:0] R7
);

  wire r0_t, r1_t, r2_t, r3_t, r4_t, r5_t, r6_t, r7_t;
  wire [31:0] AOUT_t, BOUT_t;

  Register #(.width(32)) register_1 (.D(DataIn), .en(r0_t), .clk(Clk), .Q(R0), .clr(Reset));
  Register #(.width(32)) register_2 (.D(DataIn), .en(r1_t), .clk(Clk), .Q(R1), .clr(Reset));
  Register #(.width(32)) register_3 (.D(DataIn), .en(r2_t), .clk(Clk), .Q(R2), .clr(Reset));
  Register #(.width(32)) register_4 (.D(DataIn), .en(r3_t), .clk(Clk), .Q(R3), .clr(Reset));
  Register #(.width(32)) register_5 (.D(DataIn), .en(r4_t), .clk(Clk), .Q(R4), .clr(Reset));
  Register #(.width(32)) register_6 (.D(DataIn), .en(r5_t), .clk(Clk), .Q(R5), .clr(Reset));
  Register #(.width(32)) register_7 (.D(DataIn), .en(r6_t), .clk(Clk), .Q(R6), .clr(Reset));
  Register #(.width(32)) register_8 (.D(DataIn), .en(r7_t), .clk(Clk), .Q(R7), .clr(Reset));
  Decoder #(.select(3)) decoder_1 (
    .out0(r0_t), .out1(r1_t), .out2(r2_t), .out3(r3_t), .out4(r4_t), .out5(r5_t), .out6(r6_t), .out7(r7_t),
    .sel(RegDest), .en(1'b1));
  Register #(.width(32)) register_9 (.D(AOUT_t), .en(1'b1), .clk(Clk), .Q(AOut), .clr(Reset));
  Multiplexer #(.enable("true"), .select(3), .width(32)) multiplexer_1 (
    .in0(R0), .in1(R1), .in2(R2), .in3(R3), .in4(R4), .in5(R5), .in6(R6), .in7(R7), .out(AOUT_t), .sel(RegA),
    .en(1'b1));
  Multiplexer #(.enable("true"), .select(3), .width(32)) multiplexer_2 (
    .in0(R0), .in1(R1), .in2(R2), .in3(R3), .in4(R4), .in5(R5), .in6(R6), .in7(R7), .out(BOUT_t), .sel(RegB),
    .en(1'b1));
  Register #(.width(32)) register_10 (.D(BOUT_t), .en(1'b1), .clk(Clk), .Q(BOut), .clr(Reset));

  // Other names for the same wires on the sheet: REGD[2:0] = RegDest; RST = Reset
endmodule
