// Logisim project ControleurMarius.circ as structural Verilog: 2 circuits, main circuit SP_Adresse
module SP_Adresse (
  input  [15:0] Instruction,
  input  [31:0] Stack_Pointer,
  input  Enable,
  output [31:0] New_Stack_Pointer,
  output Write_Enable
);

  wire [31:0] adder_1_out, Imm7, subtractor_1_out;

  assign Imm7 = {{25{Instruction[6]}}, Instruction[6:0]};  // Bit_Extender bit_extender_1
  Adder #(.width(32)) adder_1 (.a(Imm7), .b(Stack_Pointer), .out(adder_1_out));  // open: cin, cout
  Subtractor #(.width(32)) subtractor_1 (.a(Imm7), .b(Stack_Pointer), .out(subtractor_1_out));  // open: bin, bout
  Multiplexer #(.width(32)) multiplexer_1 (
    .in0(adder_1_out), .in1(subtractor_1_out), .out(New_Stack_Pointer), .sel(Instruction[7]));

  assign Write_Enable = Enable;

  // Other names for the same wires on the sheet: E = Enable; OP = Instruction[7]; S[31:0] = Stack_Pointer
endmodule

module Conditional (
  input  [15:0] Instruction,
  input  Enable,
  input  [3:0] Flag,
  output [10:0] Offset,
  output Verified
);

  wire CC, CS, EQ, GE, GT, HI, instuc_c, LE, LS, LT, MI, NE, PL, sortie, VC, VS;
  wire [10:0] Imm8_ext, Imm_C;

  Comparator #(.width(4)) comparator_1 (.a(4'b1101), .b(Instruction[15:12]), .eq(instuc_c));  // open: gt, lt
  Comparator #(.width(1)) comparator_2 (.a(Flag[2]), .b(1'b1), .eq(EQ));  // open: gt, lt
  Comparator #(.width(1)) comparator_3 (.a(Flag[2]), .b(1'b0), .eq(NE));  // open: gt, lt
  Comparator #(.width(1)) comparator_4 (.a(Flag[1]), .b(1'b1), .eq(CS));  // open: gt, lt
  Comparator #(.width(1)) comparator_5 (.a(Flag[1]), .b(1'b0), .eq(CC));  // open: gt, lt
  Comparator #(.width(1)) comparator_6 (.a(Flag[3]), .b(1'b1), .eq(MI));  // open: gt, lt
  Comparator #(.width(1)) comparator_7 (.a(Flag[3]), .b(1'b0), .eq(PL));  // open: gt, lt
  Comparator #(.width(1)) comparator_8 (.a(Flag[0]), .b(1'b1), .eq(VS));  // open: gt, lt
  Comparator #(.width(1)) comparator_9 (.a(Flag[0]), .b(1'b0), .eq(VC));  // open: gt, lt
  and and_1 (HI, CS, NE);
  or or_1 (LS, CC, EQ);
  Comparator #(.width(1)) comparator_10 (.a(Flag[0]), .b(Flag[3]), .eq(GE));  // open: gt, lt
  Comparator #(.width(1)) comparator_11 (.a(Flag[0]), .b(Flag[3]), .gt(LT));  // open: eq, lt
  assign Imm8_ext = {{3{Instruction[7]}}, Instruction[7:0]};  // Bit_Extender bit_extender_1
  Multiplexer #(.width(11)) multiplexer_1 (
    .in0({Instruction[11], Instruction[9:0]}), .in1(Imm8_ext), .out(Imm_C), .sel(instuc_c));
  and and_2 (GT, GE, NE);
  or or_2 (LE, LT, EQ);
  Multiplexer #(.width(11)) multiplexer_2 (.in0({11{1'b0}}), .in1(Imm_C), .out(Offset), .sel(Verified));
  Multiplexer #(.select(4)) multiplexer_3 (
    .in0(EQ), .in1(NE), .in2(CS), .in3(CC), .in4(MI), .in5(PL), .in6(VS), .in7(VC), .in8(HI), .in9(LS),
    .in10(GE), .in11(LT), .in12(GT), .in13(LE), .in14(1'b1), .in15(1'b0), .out(sortie),
    .sel(Instruction[11:8]));
  and and_3 (Verified, sortie, Enable);

  // Other names for the same wires on the sheet: cond[3:0] = Instruction[11:8]; E = Enable; V = Flag[0]; C = Flag[1];
  //   Z = Flag[2]; N = Flag[3]; Imm8[7:0] = Instruction[7:0]; Imm11[10:0] = {Instruction[11], Instruction[9:0]}
endmodule
