// Logisim project Ctl_SP_Address.circ as structural Verilog: 1 circuit, main circuit SP_Address
module SP_Address (
  input  [15:0] Instruction,
  input  Enable,
  input  [31:0] Stack_Pointer,
  output [31:0] New_Stack_Pointer,
  output Write_Enable
);

  wire [31:0] adder_1_out, bit_extender_1_out, Imm7, multiplexer_2_out, subtractor_1_out;

  assign bit_extender_1_out = {{25{1'b0}}, Instruction[6:0]};  // Bit_Extender bit_extender_1
  Shifter #(.width(32)) shifter_1 (.in(bit_extender_1_out), .\dist (5'b00010), .out(Imm7));
  Adder #(.width(32)) adder_1 (.a(Imm7), .b(Stack_Pointer), .out(adder_1_out));  // open: cin, cout
  Subtractor #(.width(32)) subtractor_1 (.a(Stack_Pointer), .b(Imm7), .out(subtractor_1_out));  // open: bin, bout
  Multiplexer #(.width(32)) multiplexer_1 (
    .in0(Stack_Pointer), .in1(multiplexer_2_out), .out(New_Stack_Pointer), .sel(Enable));
  Multiplexer #(.width(32)) multiplexer_2 (
    .in0(adder_1_out), .in1(subtractor_1_out), .out(multiplexer_2_out), .sel(Instruction[7]));

  assign Write_Enable = Enable;

  // Other names for the same wires on the sheet: E = Enable; OP = Instruction[7]; S[31:0] = Stack_Pointer
endmodule
