// Logisim project Ctl_Shift_Add_Sub_MovHabib.circ as structural Verilog: 2 circuits, main circuit Shift_Add_Sub_Mov
module Shift_Add_Sub_Mov (
  input  [15:0] Instruction,
  input  Enable,
  output [3:0] Flags_Update_Mask,
  output Carry,
  output Imm32_Enable,
  output [2:0] Rm,
  output [2:0] Rn,
  output [2:0] Rd,
  output [4:0] Imm5,
  output [31:0] Imm32,
  output [3:0] ALU_Opcode
);

  wire [1:0] SousCasAddSub, SousCasShift;
  wire [2:0] DMX, RdOURdn, RmOUIm3;
  wire [4:0] bitselector_1_out;
  wire [7:0] Imm8;

  BitSelector #(.group(5), .width(15)) bitselector_1 (.in(Instruction[15:1]), .out(bitselector_1_out), .sel(2'b10));
  BitSelector #(.group(2), .width(15)) bitselector_2 (.in(Instruction[15:1]), .out(SousCasAddSub), .sel(3'b100));
  BitSelector #(.group(2), .width(15)) bitselector_3 (.in(Instruction[15:1]), .out(SousCasShift), .sel(3'b101));
  BitSelector #(.group(3), .width(16)) bitselector_4 (.in(Instruction), .out(Rd), .sel(3'b000));
  BitSelector #(.group(3), .width(16)) bitselector_5 (.in(Instruction), .out(Rn), .sel(3'b001));
  BitSelector #(.group(3), .width(16)) bitselector_6 (.in(Instruction), .out(RmOUIm3), .sel(3'b010));
  BitSelector #(.group(8), .width(16)) bitselector_7 (.in(Instruction), .out(Imm8), .sel(1'b0));
  BitSelector #(.group(3), .width(14)) bitselector_8 (.in(Instruction[15:2]), .out(RdOURdn), .sel(3'b010));
  Choix_Op choix_op_1 (.Entree(bitselector_1_out), .E(Enable), .Cas(DMX));

  // Other names for the same wires on the sheet: ALUO[3:0] = ALU_Opcode; C = Carry; FUM[3:0] = Flags_Update_Mask;
  //   I5[4:0] = Imm5; I32[31:0] = Imm32; I32E = Imm32_Enable; instru[15:0] = Instruction

  // Notes on the sheet:
  //   only ADD and SUB use Rm
  //   Enable carry for SUB since it is reversed in ALU
  //   ALU will use Imm32 instead of Rm
endmodule

module Choix_Op (
  input  [4:0] Entree,
  input  E,
  output [2:0] Cas
);

  wire and_1_out, and_2_out, and_3_out, and_4_out, and_5_out, and_6_out, not_1_out, not_2_out, not_3_out,
       not_4_out, not_5_out, not_6_out;

  not not_1 (not_1_out, Entree[4]);
  not not_2 (not_2_out, Entree[3]);
  not not_3 (not_3_out, Entree[2]);
  not not_4 (not_4_out, Entree[1]);
  not not_5 (not_5_out, Entree[0]);
  not not_6 (not_6_out, E);
  and and_1 (and_1_out, not_1_out, not_2_out, Entree[2], Entree[0], not_6_out);
  and and_2 (and_2_out, not_1_out, not_2_out, Entree[2], Entree[1], not_6_out);
  and and_3 (and_3_out, not_1_out, not_2_out, Entree[1], Entree[0], not_6_out);
  and and_4 (and_4_out, not_1_out, not_2_out, Entree[2], not_4_out, not_5_out, not_6_out);
  and and_5 (and_5_out, not_1_out, not_2_out, not_3_out, not_4_out, not_6_out);
  and and_6 (and_6_out, not_1_out, not_2_out, not_5_out, not_6_out);
  or or_1 (Cas[2], and_1_out, and_2_out);
  or or_2 (Cas[1], and_3_out, and_4_out);
  or or_3 (Cas[0], and_5_out, and_6_out);
endmodule
