// Logisim project Ctl_Conditional.circ as structural Verilog: 1 circuit, main circuit Conditional
module Conditional (
  input  [15:0] Instruction,
  input  Enable,
  input  N,
  input  Z,
  input  C,
  input  V,
  output [10:0] Offset,
  output Verified
);

  wire CC, CS, EQ, GE, GT, HI, instuc_c, LE, LS, LT, MI, NE, or_3_out, PL, sortie, VC, VS;
  wire [10:0] Imm8_ext, Imm_C;

  Comparator #(.width(4)) comparator_1 (.a(4'b1101), .b(Instruction[15:12]), .eq(instuc_c));  // open: gt, lt
  Comparator #(.width(1)) comparator_2 (.a(Z), .b(1'b1), .eq(EQ));  // open: gt, lt
  Comparator #(.width(1)) comparator_3 (.a(Z), .b(1'b0), .eq(NE));  // open: gt, lt
  Comparator #(.width(1)) comparator_4 (.a(C), .b(1'b1), .eq(CS));  // open: gt, lt
  Comparator #(.width(1)) comparator_5 (.a(C), .b(1'b0), .eq(CC));  // open: gt, lt
  Comparator #(.width(1)) comparator_6 (.a(N), .b(1'b1), .eq(MI));  // open: gt, lt
  Comparator #(.width(1)) comparator_7 (.a(N), .b(1'b0), .eq(PL));  // open: gt, lt
  Comparator #(.width(1)) comparator_8 (.a(V), .b(1'b1), .eq(VS));  // open: gt, lt
  Comparator #(.width(1)) comparator_9 (.a(V), .b(1'b0), .eq(VC));  // open: gt, lt
  and and_1 (HI, CS, NE);
  or or_1 (LS, CC, EQ);
  Comparator #(.width(1)) comparator_10 (.a(V), .b(N), .eq(GE));  // open: gt, lt
  xor xor_1 (LT, V, N);
  assign Imm8_ext = {{3{Instruction[7]}}, Instruction[7:0]};  // Bit_Extender bit_extender_1
  Multiplexer #(.width(11)) multiplexer_1 (.in0(Instruction[10:0]), .in1(Imm8_ext), .out(Imm_C), .sel(instuc_c));
  and and_2 (GT, GE, NE);
  or or_2 (LE, LT, EQ);
  Multiplexer #(.width(11)) multiplexer_2 (.in0({11{1'b0}}), .in1(Imm_C), .out(Offset), .sel(Verified));
  Multiplexer #(.select(4)) multiplexer_3 (
    .in0(EQ), .in1(NE), .in2(CS), .in3(CC), .in4(MI), .in5(PL), .in6(VS), .in7(VC), .in8(HI), .in9(LS),
    .in10(GE), .in11(LT), .in12(GT), .in13(LE), .in14(1'b1), .in15(1'b0), .out(sortie),
    .sel(Instruction[11:8]));
  or or_3 (or_3_out, ~instuc_c, sortie);  // OR_Gate
  and and_3 (Verified, or_3_out, Enable);

  // Other names for the same wires on the sheet: cond[3:0] = Instruction[11:8]; E = Enable;
  //   Imm8[7:0] = Instruction[7:0]; Imm11[10:0] = Instruction[10:0]
endmodule
