// Logisim project Ctl_Data_Processing.circ as structural Verilog: 2 circuits, main circuit Data_Processing
module Data_Processing (
  input  Enable,
  input  [15:0] Instruction,
  output [2:0] Rd,
  output [2:0] Rn,
  output [2:0] Rm,
  output [3:0] ALU_Opcode,
  output [3:0] Flags_Update_Mask
);

  wire [2:0] briqueG;
  wire [3:0] flags_update_mask_decoder_1_s;
  wire [5:0] and_1_out;
  wire [15:0] bit_extender_1_out;

  assign bit_extender_1_out = {{15{Enable}}, Enable};  // Bit_Extender bit_extender_1
  assign {and_1_out, ALU_Opcode, briqueG, Rd} = bit_extender_1_out & Instruction;  // AND_Gate and_1, 16 bits wide
  Multiplexer #(.select(4), .width(3)) multiplexer_1 (
    .in0(briqueG), .in1(briqueG), .in2(briqueG), .in3(briqueG), .in4(briqueG), .in5(briqueG), .in6(briqueG),
    .in7(briqueG), .in8(briqueG), .in9(Rd), .in10(briqueG), .in11(briqueG), .in12(briqueG), .in13(Rd),
    .in14(briqueG), .in15(briqueG), .out(Rm), .sel(ALU_Opcode));
  Multiplexer #(.width(4)) multiplexer_2 (
    .in0(4'b0000), .in1(flags_update_mask_decoder_1_s), .out(Flags_Update_Mask), .sel(Enable));
  Flags_Update_Mask_Decoder flags_update_mask_decoder_1 (.e(ALU_Opcode), .s(flags_update_mask_decoder_1_s));
  Multiplexer #(.select(4), .width(3)) multiplexer_3 (
    .in0(Rd), .in1(Rd), .in2(Rd), .in3(Rd), .in4(Rd), .in5(Rd), .in6(Rd), .in7(Rd), .in8(Rd), .in9(briqueG),
    .in10(Rd), .in11(Rd), .in12(Rd), .in13(briqueG), .in14(Rd), .in15(Rd), .out(Rn), .sel(ALU_Opcode));

  // Other names for the same wires on the sheet: briqueD[2:0] = Rd; CasPart[3:0] = ALU_Opcode; E = Enable
endmodule

module Flags_Update_Mask_Decoder (
  input  [3:0] e,
  output [3:0] s
);

  wire and_1_out, and_2_out, and_3_out, and_4_out, not_1_out, not_2_out, not_3_out, not_4_out;

  not not_1 (not_1_out, e[3]);
  not not_2 (not_2_out, e[2]);
  not not_3 (not_3_out, e[1]);
  not not_4 (not_4_out, e[0]);
  or or_1 (s[1], not_1_out, not_2_out, not_4_out, e[1]);
  and and_1 (and_1_out, not_1_out, e[2], not_3_out, e[0]);
  and and_2 (and_2_out, not_1_out, e[2], e[1], not_4_out);
  and and_3 (and_3_out, e[3], not_2_out, e[0]);
  and and_4 (and_4_out, e[3], not_2_out, e[1]);
  or or_2 (s[0], and_1_out, and_2_out, and_3_out, and_4_out);

  assign s[3:2] = 2'b11;
endmodule
