// Logisim project Ctl_Load_Store.circ as structural Verilog: 1 circuit, main circuit Load_Store
module Load_Store (
  input  Enable,
  input  [31:0] Stack_Pointer,
  input  [15:0] Instruction,
  input  Clk,
  input  Reset,
  output [2:0] Rmd,
  output [31:0] RAM_Addr,
  output Store,
  output Load,
  output PC_Hold
);

  wire and_2_out, and_3_out, d_ff_1_q, d_ff_1_qn, not_1_out, not_2_out, or_1_out;
  wire [31:0] Add, bit_extender_1_out;

  Multiplexer multiplexer_1 (.in0(1'b0), .in1(Instruction[11]), .out(Load), .sel(Enable));
  and and_1 (Store, Enable, not_1_out);
  not not_1 (not_1_out, Load);
  Multiplexer #(.width(3)) multiplexer_2 (.in0(3'b000), .in1(Instruction[10:8]), .out(Rmd), .sel(Enable));
  not not_2 (not_2_out, d_ff_1_q);
  and and_2 (and_2_out, Instruction[11], not_2_out);
  D_Flip_Flop d_ff_1 (.D(and_2_out), .clk(Clk), .Q(d_ff_1_q), .Qn(d_ff_1_qn), .reset(or_1_out));  // open: preset
  or or_1 (or_1_out, ~Instruction[11], ~Enable, Reset);  // OR_Gate
  assign bit_extender_1_out = {{24{1'b0}}, Instruction[7:0]};  // Bit_Extender bit_extender_1
  Adder #(.width(32)) adder_1 (.a(Stack_Pointer), .b(bit_extender_1_out), .out(Add));  // open: cin, cout
  Multiplexer multiplexer_3 (.in0(1'b0), .in1(and_3_out), .out(PC_Hold), .sel(Enable));
  and and_3 (and_3_out, d_ff_1_qn, Instruction[11]);
  Multiplexer #(.width(32)) multiplexer_4 (.in0({32{1'b0}}), .in1(Add), .out(RAM_Addr), .sel(Enable));

  // Other names for the same wires on the sheet: IMM8[7:0] = Instruction[7:0]; DESTINATION[2:0] = Instruction[10:8];
  //   Code = Instruction[11]; SP[31:0] = Stack_Pointer

  // Notes on the sheet:
  //   Delay load and hold PC for 1 cycle for the RAM to send out requested data 
endmodule
