// Logisim project Ctl_Shift_Add_Sub_Mov.circ as structural Verilog: 2 circuits, main circuit Shift_Add_Sub_Mov
module Shift_Add_Sub_Mov (
  input  [15:0] Instruction,
  input  Enable,
  output [3:0] Flags_Update_Mask,
  output Carry,
  output Imm32_Enable,
  output [2:0] Rm,
  output [2:0] Rn,
  output [2:0] Rd,
  output [4:0] Imm5,
  output [31:0] Imm32,
  output [3:0] ALU_Opcode
);

  wire bitselector_10_out, bitselector_11_out, bitselector_12_out;
  wire [1:0] SousCasAddSub, SousCasShift;
  wire [2:0] MIX, multiplexer_4_out, Rd_t, Rdn, RmOUIm3, Rn_t;
  wire [3:0] OpCodeAddSub, OpCodeShift;
  wire [4:0] bitselector_1_out, imm5_t;
  wire [7:0] Imm8;
  wire [31:0] bit_extender_2_out, HT, HTI, multiplexer_5_out;

  BitSelector #(.group(5), .width(15)) bitselector_1 (.in(Instruction[15:1]), .out(bitselector_1_out), .sel(2'b10));
  BitSelector #(.group(5), .width(15)) bitselector_2 (.in(Instruction[15:1]), .out(imm5_t), .sel(2'b01));
  BitSelector #(.group(2), .width(15)) bitselector_3 (.in(Instruction[15:1]), .out(SousCasAddSub), .sel(3'b100));
  BitSelector #(.group(2), .width(15)) bitselector_4 (.in(Instruction[15:1]), .out(SousCasShift), .sel(3'b101));
  BitSelector #(.group(3), .width(16)) bitselector_5 (.in(Instruction), .out(Rd_t), .sel(3'b000));
  BitSelector #(.group(3), .width(16)) bitselector_6 (.in(Instruction), .out(Rn_t), .sel(3'b001));
  BitSelector #(.group(3), .width(16)) bitselector_7 (.in(Instruction), .out(RmOUIm3), .sel(3'b010));
  BitSelector #(.group(8), .width(16)) bitselector_8 (.in(Instruction), .out(Imm8), .sel(1'b0));
  BitSelector #(.group(3), .width(14)) bitselector_9 (.in(Instruction[15:2]), .out(Rdn), .sel(3'b010));
  Multiplexer #(.select(2), .width(4)) multiplexer_1 (
    .in0(4'b0010), .in1(4'b0011), .in2(4'b0100), .out(OpCodeShift), .sel(SousCasShift));  // open: in3
  Multiplexer #(.width(4)) multiplexer_2 (.in0(4'b0101), .in1(4'b0110), .out(OpCodeAddSub), .sel(bitselector_10_out));
  BitSelector #(.width(16)) bitselector_10 (.in(Instruction), .out(bitselector_10_out), .sel(4'b1001));
  Choix_Op choix_op_1 (.Entree(bitselector_1_out), .E(Enable), .Cas(MIX));
  Multiplexer #(.width(5)) multiplexer_3 (.in0({5{1'b0}}), .in1(imm5_t), .out(Imm5), .sel(Enable));
  assign HT = {{24{1'b0}}, Imm8};  // Bit_Extender bit_extender_1
  Negator #(.width(32)) negator_1 (.in(HT), .out(HTI));
  assign bit_extender_2_out = {{29{1'b0}}, RmOUIm3};  // Bit_Extender bit_extender_2
  BitSelector #(.width(16)) bitselector_11 (.in(Instruction), .out(bitselector_11_out), .sel(4'b1001));
  BitSelector #(.width(16)) bitselector_12 (.in(Instruction), .out(bitselector_12_out), .sel(4'b1010));
  Multiplexer #(.select(2), .width(3)) multiplexer_4 (
    .in0(RmOUIm3), .in1(RmOUIm3), .in2(3'b000), .in3(3'b000), .out(multiplexer_4_out), .sel(SousCasAddSub));
  Multiplexer #(.select(2), .width(32)) multiplexer_5 (
    .in0({32{1'b0}}), .in1({32{1'b0}}), .in2(bit_extender_2_out), .in3(bit_extender_2_out),
    .out(multiplexer_5_out), .sel(SousCasAddSub));
  Multiplexer #(.select(3), .width(4)) multiplexer_6 (
    .in0(4'b0000), .in1(4'b1110), .in2(4'b1111), .in3(4'b1100), .in4(4'b1111), .in5(4'b1111), .in6(4'b1111),
    .out(Flags_Update_Mask), .sel(MIX));  // open: in7
  Multiplexer #(.select(3)) multiplexer_7 (
    .in0(1'b0), .in1(1'b0), .in2(bitselector_11_out), .in3(1'b0), .in4(1'b0), .in5(1'b0), .in6(1'b1),
    .out(Carry), .sel(MIX));  // open: in7
  Multiplexer #(.select(3)) multiplexer_8 (
    .in0(1'b0), .in1(1'b0), .in2(bitselector_12_out), .in3(1'b1), .in4(1'b1), .in5(1'b1), .in6(1'b1),
    .out(Imm32_Enable), .sel(MIX));  // open: in7
  Multiplexer #(.select(3), .width(3)) multiplexer_9 (
    .in0(3'b000), .in1(3'b000), .in2(multiplexer_4_out), .in3(3'b000), .in4(3'b000), .in5(3'b000),
    .in6(3'b000), .out(Rm), .sel(MIX));  // open: in7
  Multiplexer #(.select(3), .width(3)) multiplexer_10 (
    .in0(3'b000), .in1(Rn_t), .in2(Rn_t), .in3(3'b000), .in4(Rdn), .in5(Rdn), .in6(Rdn), .out(Rn), .sel(MIX));  // open: in7
  Multiplexer #(.select(3), .width(3)) multiplexer_11 (
    .in0(3'b000), .in1(Rd_t), .in2(Rd_t), .in3(Rdn), .in4(Rdn), .in5(Rdn), .in6(Rdn), .out(Rd), .sel(MIX));  // open: in7
  Multiplexer #(.select(3), .width(32)) multiplexer_12 (
    .in0({32{1'b0}}), .in1({32{1'b0}}), .in2(multiplexer_5_out), .in3(HTI), .in4(HT), .in5(HT), .in6(HT),
    .out(Imm32), .sel(MIX));  // open: in7
  Multiplexer #(.select(3), .width(4)) multiplexer_13 (
    .in0(4'b0000), .in1(OpCodeShift), .in2(OpCodeAddSub), .in3(4'b1001), .in4(4'b1010), .in5(4'b0101),
    .in6(4'b0110), .out(ALU_Opcode), .sel(MIX));  // open: in7

  // Other names for the same wires on the sheet: ALUO[3:0] = ALU_Opcode; C = Carry; E = Enable;
  //   FUM[3:0] = Flags_Update_Mask; I32[31:0] = Imm32; I32E = Imm32_Enable; imm5S[4:0] = Imm5;
  //   instru[15:0] = Instruction; RdS[2:0] = Rd; RmS[2:0] = Rm; RnS[2:0] = Rn

  // Notes on the sheet:
  //   only ADD and SUB use Rm
  //   Enable carry for SUB since it is reversed in ALU
  //   ALU will use Imm32 instead of Rm
endmodule

module Choix_Op (
  input  [4:0] Entree,
  input  E,
  output [2:0] Cas
);

  wire and_1_out, and_2_out, and_3_out, and_4_out, and_5_out, and_6_out, not_1_out, not_2_out, not_3_out,
       not_4_out, not_5_out;

  not not_1 (not_1_out, Entree[4]);
  not not_2 (not_2_out, Entree[3]);
  not not_3 (not_3_out, Entree[2]);
  not not_4 (not_4_out, Entree[1]);
  not not_5 (not_5_out, Entree[0]);
  and and_1 (and_1_out, not_1_out, not_2_out, Entree[2], Entree[0], E);
  and and_2 (and_2_out, not_1_out, not_2_out, Entree[2], Entree[1], E);
  and and_3 (and_3_out, not_1_out, not_2_out, Entree[1], Entree[0], E);
  and and_4 (and_4_out, not_1_out, not_2_out, Entree[2], not_4_out, not_5_out, E);
  and and_5 (and_5_out, not_1_out, not_2_out, not_3_out, not_4_out, E);
  and and_6 (and_6_out, not_1_out, not_2_out, not_5_out, E);
  or or_1 (Cas[2], and_1_out, and_2_out);
  or or_2 (Cas[1], and_3_out, and_4_out);
  or or_3 (Cas[0], and_5_out, and_6_out);
endmodule
